# Fritzing sketch snake-nxn (saved by Fritzing 0.9.3b)
breadboards: 1

parts:
  Part5 = Arduino Mega 2560 (Rev3)
  Part6 = NeoPixel NeoMatrix 8x8 [part_number=1487]  # not connected
  YwRobot_Power_Supply2 = YwRobot Breadboard Power Supply [part_number=545043]
  Part7 = Adafruit Analog 2-Axis Joystick [part_number="Adafruit #512"]

nets:
  N1: Part5.A0, Part7.XOUT
  N2: Part5.A1, Part7.YOUT
  GND: Part5.GND, YwRobot_Power_Supply2.GND, Part7.GND
  5V: Part5.5V, Part7.VCC
  N3: Part5.D7_PWM, Part7.SWITCH

custom parts:
  NeoPixel NeoMatrix 8x8: Put on your sunglasses before wiring up this LED matrix - 64 eye-blistering RGB LEDs adorn the NeoMatrix for a blast of configurable color. Arranged in an 8x8 matrix, each pixel is individually addressable. Only one microcontroller pin is required to control all the LEDs, and you get 24 bit color for each LED.
  YwRobot Breadboard Power Supply: The YwRobot Breadboard Power Supply (MB-V2) has two power rails; they can be 5V or 3V3. Power to the module can be provided through the female USB socket or through the A10 (female) 2.1mm power jack.
  Adafruit Analog 2-Axis Joystick: This mini-kit makes it easy to mount a PSP/Xbox-like thumb joystick to your project. The thumbstick is an analog joystick - more accurate and sensitive than just 'directional' joysticks - with a 'press in to select' button. Since it's analog, you'll need two analog reading pins on your microcontroller to determine X and Y. Having an extra digital input will let you read the switch. The pack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
